# Fritzing sketch esp32 LoRa emisor (saved by Fritzing 0.9.3b)
breadboards: 1

parts:
  Heltec_WiFi_LoRa_32_V3 = Heltec WiFi LoRa 32 V2 [part_number=HTIT-WB32LA]
  S1 = Momentary Switch [package=ksa_sealed_tac_switch]
  R3 = Resistor [tolerance=±5% resistance=10k package=THT]

nets:
  N1: Heltec_WiFi_LoRa_32_V3.pin_13, S1.4, R3.Pin_1
  N2: Heltec_WiFi_LoRa_32_V3.pin_16, Heltec_WiFi_LoRa_32_V3.pin_17
  N3: Heltec_WiFi_LoRa_32_V3.pin_18, Heltec_WiFi_LoRa_32_V3.pin_19, R3.Pin_0
  N4: Heltec_WiFi_LoRa_32_V3.pin_20, S1.2
  N5: Heltec_WiFi_LoRa_32_V3.pin_21, Heltec_WiFi_LoRa_32_V3.pin_22

custom parts:
  Heltec WiFi LoRa 32 V2: Heltec WiFi LoRa 32 V2 WiFi LoRa 32 is a classic IoT dev-board designed & produced by Heltec Automation(TM). It’s a highly integrated product based on ESP32 + SX127x, it has Wi-Fi, BLE, LoRa functions, also Li-Po battery management system, 0.96″ OLED are also included. It’s the best choice for smart cities, smart farms, smart home, and IoT makers.
